# Fritzing sketch ZuikakuD3A2 (saved by Fritzing 1.0.7)
breadboards: 1

parts:
  U1 = 555 Timer [package="DIP8 [THT]"]
  R1 = Resistor [tolerance=±5% resistance=1k power=0.25W package=THT]
  R2 = Trimmer Potentiometer [maximum_resistance=50kΩ knob_status=50% power=0.5W package=THT]
  D1 = Rectifier Diode [part_number=1N4148 package="300 mil [THT]"]
  D2 = Rectifier Diode [part_number=1N4148 package="300 mil [THT]"]
  C5 = Ceramic Capacitor [capacitance=1.5nF voltage=35V package="100 mil [THT, multilayer]"]
  3V = LilyPad Coin Cell Battery Holder
  M1 = DC Motor [voltage_(max)=6V voltage_(min)=3V]
  D3 = Rectifier Diode [part_number=1N4001 package="300 mil [THT]"]

nets:
  GND: U1.Ground, C5.1, 3V.-, M1.pin_2, D3.anode
  N1: U1.Trigger, U1.Threshold, R2.wiper, C5.0
  OUT (PWM): U1.Output, M1.pin_1, D3.cathode
  VCC: U1.Reset, U1.Vcc_Supply_Voltage, R1.Pin_0, 3V.+
  N2: U1.Discharge, R1.Pin_1, D1.anode, D2.cathode
  N3: R2.leg1, D2.anode
  N4: R2.leg2, D1.cathode
