# Fritzing sketch ScopeDog (saved by Fritzing 1.0.1rc)
breadboards: 1

parts:
  U1 = 555 Timer [package="DIP8 [THT]"]
  3-5V = Power plug
  C1 = Electrolytic Capacitor [capacitance=10µF voltage=35V package="100 mil [THT, electrolytic]"]
  R1 = Resistor [tolerance=±5% resistance=2k power=0.25W package=THT]
  RL1 = Resistor [tolerance=±5% resistance=220 power=0.25W package=THT]
  RL2 = Resistor [tolerance=±5% resistance=220 power=0.25W package=THT]
  RL3 = Resistor [tolerance=±5% resistance=220 power=0.25W package=THT]
  RL4 = Resistor [tolerance=±5% resistance=220 power=0.25W package=THT]
  RL5 = Resistor [tolerance=±5% resistance=220 power=0.25W package=THT]
  U2 = IC, DIP package, 16 pins [chip_label=CD4017 part_number=CD4017]
  S1 = Toggle Switch [package=THT]
  LED1 = LED - 3mm [color="Red (633nm)" current=0.030A package="3 mm [THT]"]
  LED2 = LED - 3mm [color="Red (633nm)" current=0.030A package="3 mm [THT]"]
  LED3 = LED - 3mm [color="Red (633nm)" current=0.030A package="3 mm [THT]"]
  LED4 = LED - 3mm [color="Red (633nm)" current=0.030A package="3 mm [THT]"]
  LED5 = LED - 3mm [color="Red (633nm)" current=0.030A package="3 mm [THT]"]
  R2 = Resistor [tolerance=±5% power=0.25W resistance=10k package=THT]

nets:
  GND: U1.Ground, 3-5V.GND, C1.-, U2.pin8, U2.pin13, U2.pin15, LED1.cathode, LED2.cathode, LED3.cathode, LED4.cathode, LED5.cathode
  N1: U1.Trigger, U1.Threshold, C1.+, R2.Pin_1
  CLK: U1.Output, U2.pin14
  VCC: U1.Reset, U1.Vcc_Supply_Voltage, R1.Pin_1, U2.pin16, S1.L2
  N2: U1.Discharge, R1.Pin_0, R2.Pin_0
  N3: 3-5V.VCC, S1.COM
  N4: RL1.Pin_0, LED1.anode
  L0: RL1.Pin_1, U2.pin3
  N5: RL2.Pin_0, LED2.anode
  L2: RL2.Pin_1, U2.pin4
  N6: RL3.Pin_0, LED3.anode
  L4: RL3.Pin_1, U2.pin10
  N7: RL4.Pin_0, LED4.anode
  L5: RL4.Pin_1, U2.pin1
  N8: RL5.Pin_0, LED5.anode
  L8: RL5.Pin_1, U2.pin9

notes:
  up to 5 LEDs per output
